// Digital circuit 1bitaddernoxor.dig as structural Verilog
module _1bitaddernoxor (
  input  A,
  input  B,
  input  C,
  output SUM,
  output Carry
);

  wire and_1_out, and_2_out, and_3_out, and_4_out, and_5_out, and_6_out, not_1_out, not_2_out, not_3_out,
       not_4_out, or_1_out;

  not not_1 (not_1_out, A);
  not not_2 (not_2_out, B);
  and and_1 (and_1_out, not_1_out, B);
  and and_2 (and_2_out, A, not_2_out);
  and and_3 (and_3_out, A, B);
  or or_1 (or_1_out, and_1_out, and_2_out);
  not not_3 (not_3_out, C);
  not not_4 (not_4_out, or_1_out);
  and and_4 (and_4_out, C, or_1_out);
  and and_5 (and_5_out, not_3_out, or_1_out);
  and and_6 (and_6_out, C, not_4_out);
  or or_2 (SUM, and_5_out, and_6_out);
  or or_3 (Carry, and_4_out, and_3_out);
endmodule
