// Digital circuit 2bitmultiplier.dig as structural Verilog
module _2bitmultiplier (
  input  b1,
  input  a1,
  input  b0,
  input  a1_2,
  input  b1_2,
  input  a0,
  input  b0_2,
  input  a0_2,
  output p3,
  output p2,
  output p1,
  output p0
);

  wire and_1_out, and_2_out, and_3_out, and_5_out;

  and and_1 (and_1_out, b1, a1);
  and and_2 (and_2_out, b0, a1_2);
  and and_3 (and_3_out, b1_2, a0);
  and and_4 (p0, b0_2, a0_2);
  and and_5 (and_5_out, and_2_out, and_3_out);
  xor xor_1 (p1, and_2_out, and_3_out);
  and and_6 (p3, and_1_out, and_5_out);
  xor xor_2 (p2, and_1_out, and_5_out);
endmodule
