// Digital circuit 4bitaddernoxor.dig as structural Verilog
module _4bitaddernoxor (
  input  [3:0] A,
  input  [3:0] B,
  output [3:0] SUM,
  output OverFlow_flag
);

  wire _1bitaddernoxor_2_carry, _1bitaddernoxor_3_carry, _1bitaddernoxor_4_carry;

  _1bitaddernoxor _1bitaddernoxor_1 (
    .A(_1bitaddernoxor_2_carry), .B(B[3]), .C(A[3]), .SUM(SUM[3]), .Carry(OverFlow_flag));
  _1bitaddernoxor _1bitaddernoxor_2 (
    .A(_1bitaddernoxor_3_carry), .B(B[2]), .C(A[2]), .SUM(SUM[2]), .Carry(_1bitaddernoxor_2_carry));
  _1bitaddernoxor _1bitaddernoxor_3 (
    .A(_1bitaddernoxor_4_carry), .B(B[1]), .C(A[1]), .SUM(SUM[1]), .Carry(_1bitaddernoxor_3_carry));
  _1bitaddernoxor _1bitaddernoxor_4 (.A(1'b0), .B(A[0]), .C(B[0]), .SUM(SUM[0]), .Carry(_1bitaddernoxor_4_carry));
endmodule
