// Digital circuit adder.dig as structural Verilog
module adder (
  input  C,
  input  B,
  input  A,
  output Y,
  output X
);

  wire and_1_out, and_2_out, xor_1_out;

  and and_1 (and_1_out, A, B);
  xor xor_1 (xor_1_out, A, B);
  and and_2 (and_2_out, xor_1_out, C);
  xor xor_2 (Y, xor_1_out, C);
  or or_1 (X, and_2_out, and_1_out);
endmodule
