// Digital circuit adder2.dig as structural Verilog
module adder2 (
  input  [3:0] A,
  input  [3:0] B,
  output [3:0] SUM,
  output OverFlow_flag
);

  wire adder_2_x, adder_3_x, adder_4_x;

  adder adder_1 (.C(adder_2_x), .B(B[3]), .A(A[3]), .Y(SUM[3]), .X(OverFlow_flag));
  adder adder_2 (.C(adder_3_x), .B(B[2]), .A(A[2]), .Y(SUM[2]), .X(adder_2_x));
  adder adder_3 (.C(adder_4_x), .B(B[1]), .A(A[1]), .Y(SUM[1]), .X(adder_3_x));
  adder adder_4 (.C(1'b0), .B(A[0]), .A(B[0]), .Y(SUM[0]), .X(adder_4_x));
endmodule
